# Fritzing sketch MIX04_Test (saved by Fritzing 0.9.4)
breadboards: 1

parts:
  IC1 = Dual Op-Amp [package=dip08]
  R2 = Resistor [tolerance=±5% resistance=68k package=THT]
  R3 = Rotary Potentiometer (Small) [maximum_resistance=100kΩ package=THT]
  R4 = Resistor [tolerance=±5% resistance=68k package=THT]
  R5 = Rotary Potentiometer (Small) [maximum_resistance=100kΩ package=THT]
  R6 = Resistor [tolerance=±5% resistance=470k package=THT]
  R7 = Rotary Potentiometer (Small) [maximum_resistance=100kΩ package=THT]
  R8 = Resistor [tolerance=±5% resistance=10k package=THT]
  R9 = Resistor [tolerance=±5% resistance=1k package=THT]
  C1 = Ceramic Capacitor [capacitance=100nF package="100 mil [THT, multilayer]"]
  C2 = Ceramic Capacitor [capacitance=100nF package="100 mil [THT, multilayer]"]
  C3 = Electrolytic Capacitor [capacitance=1µF package="100 mil [THT, electrolytic]"]
  C4 = Electrolytic Capacitor [capacitance=1µF package="100 mil [THT, electrolytic]"]
  IC2 = Dual Op-Amp [package=dip08]
  R10 = Resistor [tolerance=±5% resistance=100k package=THT]
  R11 = Resistor [tolerance=±5% resistance=100k package=THT]
  C5 = Ceramic Capacitor [capacitance=100nF package="100 mil [THT, multilayer]"]
  C6 = Ceramic Capacitor [capacitance=100nF package="100 mil [THT, multilayer]"]
  R12 = Resistor [tolerance=±5% resistance=22k package=THT]
  R13 = Resistor [tolerance=±5% resistance=567k package=THT]
  R14 = Resistor [tolerance=±5% resistance=56k package=THT]
  R15 = Resistor [tolerance=±5% resistance=1k package=THT]

nets:
  N1: IC1.A_OUT, R6.Pin_1, R8.Pin_1
  N2: IC1.A_-IN, R2.Pin_1, R4.Pin_1, R6.Pin_0
  N3: IC1.A_+IN, C2.0, R12.Pin_0
  N4: IC1.A_V-, C2.1, C4.-, IC2.A_V-, C6.1
  N5: IC1.B_+IN, R13.Pin_1
  N6: IC1.B_-IN, R7.wiper
  N7: IC1.B_OUT, R7.leg1, R9.Pin_1
  N8: IC1.A_V+, C1.0, C3.+, IC2.A_V+, C5.0
  N9: R2.Pin_0, R3.wiper
  N10: R3.leg1, R5.leg1, C1.1, C3.-, C4.+, IC2.A_+IN, C5.1, C6.0, R12.Pin_1, R13.Pin_0, R14.Pin_0
  N11: R4.Pin_0, R5.wiper
  N12: R7.leg2, R8.Pin_0
  N13: R9.Pin_0, R11.Pin_1
  N14: IC2.A_OUT, IC2.A_-IN
  N15: IC2.B_+IN, R14.Pin_1
  N16: IC2.B_-IN, R10.Pin_1, R11.Pin_0
  N17: IC2.B_OUT, R10.Pin_0, R15.Pin_1

notes:
  GND
  V+
  V-
  GND
  OUT
  IN1
  IN2
  INV
  50k/B
  50k/A
